// Logisim project ex1.circ as structural Verilog: 1 circuit, main circuit main
module main (
  input  in_1,
  input  in_2,
  output out_3
);

  wire nand_1_out;

  // AND_Gate and_1 has open pins: in0=in_1, in1=in_2, out=open
  nand nand_1 (nand_1_out, in_1, in_2);
  not not_1 (out_3, nand_1_out);

  // Notes on the sheet:
  //   Wong Wai Chun & 1155173231
endmodule
