// Logisim project ex2.circ as structural Verilog: 1 circuit, main circuit main
module main (
  input  A,
  input  B,
  input  C,
  input  D,
  output X
);

  wire nand_1_out, nand_2_out, nand_3_out, or_1_out;

  nand nand_1 (nand_1_out, A, B);
  nand nand_2 (nand_2_out, B, C);
  nand nand_3 (nand_3_out, nand_1_out, nand_1_out);
  or or_1 (or_1_out, nand_3_out, nand_2_out);
  or or_2 (X, or_1_out, D);

  // Notes on the sheet:
  //   F
  //   E
  //   Wong Wai Chun & 1155173231
  //   G
endmodule
