// Logisim project lab2.circ as structural Verilog: 1 circuit, main circuit main
module main (
  input  A,
  input  B,
  input  C,
  input  D
);

  wire nor_1_out, nor_2_out, nor_3_out, nor_4_out;

  nor nor_1 (nor_1_out, B, C);
  nor nor_2 (nor_2_out, D, B);
  not nor_3 (nor_3_out, nor_1_out);  // NOR_Gate
  _7_Segment_Display u_7_segment_display_1 (
    .g(nor_3_out), .f(B), .a(C), .b(1'b1), .e(nor_2_out), .d(C), .c(nor_4_out));  // open: dp
  nor nor_4 (nor_4_out, nor_2_out, nor_2_out);

  // Notes on the sheet:
  //   Wong Wai Chun 1155173231
endmodule
