// Logisim project 1-bit full-adder.circ as structural Verilog: 1 circuit, main circuit main
module main (
  input  A,
  input  B,
  input  Ci,
  output S,
  output Co
);

  wire and_1_out, and_2_out, xor_1_out;

  xor xor_1 (xor_1_out, A, B);
  xor xor_2 (S, xor_1_out, Ci);
  and and_1 (and_1_out, xor_1_out, Ci);
  and and_2 (and_2_out, B, A);
  or or_1 (Co, and_1_out, and_2_out);

  // Notes on the sheet:
  //   Wong Wai Chun 1155173231
endmodule
