// Logisim project 2-bit full adder.circ as structural Verilog: 1 circuit, main circuit main
module main (
  input  A,
  input  B,
  input  Ci,
  input  A1,
  input  B1,
  output S,
  output S1,
  output C1
);

  wire and_1_out, and_2_out, and_3_out, and_4_out, or_1_out, xor_1_out, xor_2_out;

  xor xor_1 (xor_1_out, A, B);
  xor xor_2 (xor_2_out, A1, B1);
  xor xor_3 (S, xor_1_out, Ci);
  and and_1 (and_1_out, xor_1_out, Ci);
  and and_2 (and_2_out, B, A);
  xor xor_4 (S1, xor_2_out, or_1_out);
  and and_3 (and_3_out, xor_2_out, or_1_out);
  and and_4 (and_4_out, B1, A1);
  or or_1 (or_1_out, and_1_out, and_2_out);
  or or_2 (C1, and_3_out, and_4_out);

  // Notes on the sheet:
  //   Wong Wai Chun 1155173231
  //   Co
endmodule
