// Logisim project lab4.circ as structural Verilog: 1 circuit, main circuit main
module main (
  input  reset,
  output Q0,
  output Q1,
  output Q0_2,
  output Q1_2,
  output Q2,
  output Q3,
  output Q4,
  output Q5
);

  wire clock_1_out, clock_2_out, not_1_out, not_2_out, reset_out, t_ff_1_qn, t_ff_2_qn, t_ff_3_qn, t_ff_5_qn,
       t_ff_6_qn, t_ff_7_qn;

  Clock clock_1 (.out(clock_1_out));
  Clock clock_2 (.out(clock_2_out));
  and u_reset (reset_out, Q5, Q4, Q3, not_2_out, not_1_out);
  T_Flip_Flop t_ff_1 (.clk(clock_1_out), .T(1'b1), .Q(Q0), .Qn(t_ff_1_qn), .reset(reset));  // open: preset, en
  T_Flip_Flop t_ff_2 (.clk(clock_2_out), .T(1'b1), .Q(Q0_2), .Qn(t_ff_2_qn), .reset(reset_out));  // open: preset, en
  T_Flip_Flop t_ff_3 (.clk(t_ff_2_qn), .T(1'b1), .Q(Q1_2), .Qn(t_ff_3_qn), .reset(reset_out));  // open: preset, en
  not not_1 (not_1_out, Q0_2);
  T_Flip_Flop t_ff_4 (.clk(t_ff_1_qn), .T(1'b1), .Q(Q1), .reset(reset));  // open: Qn, preset, en
  not not_2 (not_2_out, Q1_2);
  T_Flip_Flop t_ff_5 (.clk(t_ff_3_qn), .T(1'b1), .Q(Q2), .Qn(t_ff_5_qn), .reset(reset_out));  // open: preset, en
  T_Flip_Flop t_ff_6 (.clk(t_ff_5_qn), .T(1'b1), .Q(Q3), .Qn(t_ff_6_qn), .reset(reset_out));  // open: preset, en
  T_Flip_Flop t_ff_7 (.clk(t_ff_6_qn), .T(1'b1), .Q(Q4), .Qn(t_ff_7_qn), .reset(reset_out));  // open: preset, en
  T_Flip_Flop t_ff_8 (.clk(t_ff_7_qn), .T(1'b1), .Q(Q5), .reset(reset_out));  // open: Qn, preset, en

  // Notes on the sheet:
  //   Q1
  //   Clock
  //   constant
  //   Q2
  //   N=6, 2^6 =64
  //   Q3
  //   Q4
  //   clock
  //   constant 1
  //   X = Q5Q4Q3Q2(Q1)'(Q0)'
  //   1155173231 Wong Wai Chun
endmodule
